# Fritzing sketch mfrc-522-node (saved by Fritzing 0.9.3b)

parts:
  U1 = RFID RC522 SIP - 8 pins [chip_label="RFID RC522" package="SIP (Single Inline) [THT]"]
  Raspberry_Pi_1 = Raspberry Pi 3 [part_number=RPI-3-V1.2]
  IC1 = Voltage Regulator AMS1117 [package=sot223]
  R1 = Resistor [tolerance=±5% resistance=1k package=THT]
  U2 = TRANSISTOR_NPN_2 [package=to-92]
  J1 = Piezo Speaker
  IC2 = Voltage Regulator AMS1117 [package=sot223]  # not connected

nets:
  N1: U1.NSS, Raspberry_Pi_1.GIPO8
  N2: U1.SCK, Raspberry_Pi_1.GIPO11
  N3: U1.MOSI, Raspberry_Pi_1.GIPO10
  N4: U1.MISO, Raspberry_Pi_1.GIPO9
  GND: U1.GND, Raspberry_Pi_1.GND, IC1.GND, J1.pin1
  N5: U1.RST, Raspberry_Pi_1.GIPO25
  N6: U1.VCC, IC1.OUT
  N7: Raspberry_Pi_1.GIPO24, R1.Pin_1
  N8: Raspberry_Pi_1.5V, IC1.IN, U2.E
  N9: R1.Pin_0, U2.B
  N10: U2.C, J1.pin2

notes:
  1kΩ Better safty but
  tested with (330Ω)
  S8050 (NPN)
  5V Buzzer active (NOT Passive)
  AMS1117 5V to 3.3V step down regulator

custom parts:
  RFID RC522 SIP - 8 pins: A SIP stand-in part for RFID RC522 . With 8 pins on a 300 mil single inline package (SIP) footprint.
